// Logisim project computer_clark.circ as structural Verilog
module mem_bit (
  input  in_1,
  input  in_2,
  output out_3
);

  wire nand_transistores_4_1_out_3, nand_transistores_4_2_out_3, nand_transistores_4_4_out_3;

  nand_transistores_4 nand_transistores_4_1 (.in_1(in_1), .in_2(in_2), .out_3(nand_transistores_4_1_out_3));
  nand_transistores_4 nand_transistores_4_2 (
    .in_1(nand_transistores_4_1_out_3), .in_2(in_2), .out_3(nand_transistores_4_2_out_3));
  nand_transistores_4 nand_transistores_4_3 (
    .in_1(nand_transistores_4_1_out_3), .in_2(nand_transistores_4_4_out_3), .out_3(out_3));
  nand_transistores_4 nand_transistores_4_4 (
    .in_1(out_3), .in_2(nand_transistores_4_2_out_3), .out_3(nand_transistores_4_4_out_3));

  // Notes on the sheet:
  //   in_2: pull=up, initial=0x1
endmodule

module mem_byte (
  input  in_1,
  input  in_2,
  input  in_3,
  input  in_4,
  input  in_5,
  input  in_6,
  input  in_7,
  input  in_8,
  input  in_9,
  output out_10,
  output out_11,
  output out_12,
  output out_13,
  output out_14,
  output out_15,
  output out_16,
  output out_17
);

  mem_bit mem_bit_1 (.in_1(in_1), .in_2(in_9), .out_3(out_10));
  mem_bit mem_bit_2 (.in_1(in_2), .in_2(in_9), .out_3(out_11));
  mem_bit mem_bit_3 (.in_1(in_3), .in_2(in_9), .out_3(out_12));
  mem_bit mem_bit_4 (.in_1(in_4), .in_2(in_9), .out_3(out_13));
  mem_bit mem_bit_5 (.in_1(in_5), .in_2(in_9), .out_3(out_14));
  mem_bit mem_bit_6 (.in_1(in_6), .in_2(in_9), .out_3(out_15));
  mem_bit mem_bit_7 (.in_1(in_7), .in_2(in_9), .out_3(out_16));
  mem_bit mem_bit_8 (.in_1(in_8), .in_2(in_9), .out_3(out_17));

  // Notes on the sheet:
  //   in_9: initial=0x1
  //   input
  //   set
  //   output
endmodule

module prueba_mem_byte (
  input  in_1,
  input  in_2,
  input  in_3
);

  wire dipswitch_1_p1, dipswitch_1_p2, dipswitch_1_p3, dipswitch_1_p4, dipswitch_1_p5, dipswitch_1_p6,
       dipswitch_1_p7, dipswitch_1_p8, dipswitch_1_p18, dipswitch_1_p19, dipswitch_1_p20, dipswitch_1_p21,
       dipswitch_1_p22, dipswitch_1_p23, dipswitch_1_p24, dipswitch_1_p25, mem_bit_1_out_3;

  mem_bit mem_bit_1 (.in_1(in_1), .in_2(in_2), .out_3(mem_bit_1_out_3));
  LED led_1 (.in(mem_bit_1_out_3));
  // DipSwitch dipswitch_1: pin names not known; wires that end beside it: dipswitch_1_p1, dipswitch_1_p2, dipswitch_1_p3, dipswitch_1_p4, dipswitch_1_p5, dipswitch_1_p6, dipswitch_1_p7, dipswitch_1_p8, dipswitch_1_p1, dipswitch_1_p2, dipswitch_1_p3, dipswitch_1_p4, dipswitch_1_p5, dipswitch_1_p6, dipswitch_1_p7, dipswitch_1_p8, in_3, dipswitch_1_p18, dipswitch_1_p19, dipswitch_1_p20, dipswitch_1_p21, dipswitch_1_p22, dipswitch_1_p23, dipswitch_1_p24, dipswitch_1_p25
  LedBar ledbar_1 (
    .led0(dipswitch_1_p18), .led1(dipswitch_1_p19), .led2(dipswitch_1_p20), .led3(dipswitch_1_p21),
    .led4(dipswitch_1_p22), .led5(dipswitch_1_p23), .led6(dipswitch_1_p24), .led7(dipswitch_1_p25));

  // Notes on the sheet:
  //   in_2: initial=0x1
  //   Memoria de 1 bit
  //   Memoria de 1 byte
endmodule

module nand_transistores_2 (
  input  in_1,
  input  in_2,
  output out_3
);

  Transistor transistor_1 (.in(1'b1), .out(out_3), .gate(in_1));
  Pull_Resistor #(.pull(1)) pull_resistor_1 (.node(out_3));
  Transistor transistor_2 (.in(1'b1), .out(out_3), .gate(in_2));
  Pull_Resistor #(.pull(1)) pull_resistor_2 (.node(out_3));

  // Notes on the sheet:
  //   in_1: pull=up
  //   in_2: pull=up
  //   out_3: pull=up
endmodule

module prueba_mem_bit (
  input  in_1,
  input  in_2
);

  wire mem_bit_1_out_3;

  mem_bit mem_bit_1 (.in_1(in_1), .in_2(in_2), .out_3(mem_bit_1_out_3));
  LED led_1 (.in(mem_bit_1_out_3));

  // Notes on the sheet:
  //   in_2: initial=0x1
  //   Memoria de 1 bit
endmodule

module nand_transistores_3 (
  input  in_1,
  input  in_2,
  output out_3
);

  wire transistor_1_out, transistor_4_out;

  Transistor transistor_1 (.in(1'b1), .out(transistor_1_out), .gate(in_1));
  Transistor transistor_2 (.in(1'b1), .out(transistor_1_out), .gate(in_2));
  buf buffer_1 (out_3, transistor_1_out);
  Transistor #(.\type ("n")) transistor_3 (.in(transistor_4_out), .out(transistor_1_out), .gate(in_1));
  Transistor #(.\type ("n")) transistor_4 (.in(1'b0), .out(transistor_4_out), .gate(in_2));
endmodule

module nand_transistores_4 (
  input  in_1,
  input  in_2,
  output out_3
);

  wire transistor_1_out;

  Transistor #(.\type ("n")) transistor_1 (.in(1'b0), .out(transistor_1_out), .gate(in_1));
  Pull_Resistor #(.pull(1)) pull_resistor_1 (.node(transistor_1_out));
  Transistor #(.\type ("n")) transistor_2 (.in(transistor_1_out), .out(out_3), .gate(in_2));
  Pull_Resistor #(.pull(1)) pull_resistor_2 (.node(out_3));

  // Notes on the sheet:
  //   in_2: initial=0x1
endmodule
